// Logisim project ALU.circ as structural Verilog: 29 circuits, main circuit main
module main (
  input  [7:0] in_1,
  input  in_2,
  input  in_3
);

  reg2 reg2_1 (.D(in_1), .S(in_2), .E(in_3));  // open: O
  reg1 reg1_1 ();  // open: O, S, E, D
endmodule

module d_latch (
  input  D,
  input  E,
  output Q,
  output NQ
);

  wire nand_1_out, nand_2_out;

  nand nand_1 (nand_1_out, D, E);
  nand nand_2 (nand_2_out, nand_1_out, E);
  LED led_1 (.in(Q));
  nand nand_3 (Q, nand_1_out, NQ);
  nand nand_4 (NQ, Q, nand_2_out);

  // Notes on the sheet:
  //   Occurred error in feedback wiring 
  //   Use D flip-flop
endmodule

module enabler (
  input  [7:0] i,
  input  e,
  output [7:0] o
);

  wire [7:0] and_1_out;

  and and_1 (and_1_out[0], i[0], e);
  and and_2 (and_1_out[1], i[1], e);
  and and_3 (and_1_out[2], i[2], e);
  and and_4 (and_1_out[3], i[3], e);
  and and_5 (and_1_out[4], i[4], e);
  and and_6 (and_1_out[5], i[5], e);
  and and_7 (and_1_out[6], i[6], e);
  and and_8 (and_1_out[7], i[7], e);
  assign o = e ? and_1_out : 8'bz;  // Controlled_Buffer controlled_buffer_1

  // Notes on the sheet:
  //   Use controlled buffer with 8bit witdth !
endmodule

module reg1 (
  input  [7:0] D,
  input  S,
  input  E,
  output [7:0] O
);

  wire [7:0] d_latch_8_q;

  d_latch d_latch_1 (.Q(d_latch_8_q[7]), .E(S), .D(D[7]));  // open: NQ
  d_latch d_latch_2 (.Q(d_latch_8_q[6]), .E(S), .D(D[6]));  // open: NQ
  d_latch d_latch_3 (.Q(d_latch_8_q[5]), .E(S), .D(D[5]));  // open: NQ
  d_latch d_latch_4 (.Q(d_latch_8_q[4]), .E(S), .D(D[4]));  // open: NQ
  d_latch d_latch_5 (.Q(d_latch_8_q[3]), .E(S), .D(D[3]));  // open: NQ
  d_latch d_latch_6 (.Q(d_latch_8_q[2]), .E(S), .D(D[2]));  // open: NQ
  d_latch d_latch_7 (.Q(d_latch_8_q[1]), .E(S), .D(D[1]));  // open: NQ
  d_latch d_latch_8 (.Q(d_latch_8_q[0]), .E(S), .D(D[0]));  // open: NQ
  assign O = E ? d_latch_8_q : 8'bz;  // Controlled_Buffer controlled_buffer_1
endmodule

module reg2 (
  input  [7:0] D,
  input  S,
  input  E,
  output [7:0] O
);

  wire [7:0] d_ff_1_q;

  D_Flip_Flop #(.trigger("high")) d_ff_1 (.D(D[0]), .clk(S), .Q(d_ff_1_q[0]));  // open: Qn, preset, reset
  D_Flip_Flop #(.trigger("high")) d_ff_2 (.D(D[1]), .clk(S), .Q(d_ff_1_q[1]));  // open: Qn, preset, reset
  D_Flip_Flop #(.trigger("high")) d_ff_3 (.D(D[2]), .clk(S), .Q(d_ff_1_q[2]));  // open: Qn, preset, reset
  D_Flip_Flop #(.trigger("high")) d_ff_4 (.D(D[3]), .clk(S), .Q(d_ff_1_q[3]));  // open: Qn, preset, reset
  D_Flip_Flop #(.trigger("high")) d_ff_5 (.D(D[4]), .clk(S), .Q(d_ff_1_q[4]));  // open: Qn, preset, reset
  D_Flip_Flop #(.trigger("high")) d_ff_6 (.D(D[5]), .clk(S), .Q(d_ff_1_q[5]));  // open: Qn, preset, reset
  D_Flip_Flop #(.trigger("high")) d_ff_7 (.D(D[6]), .clk(S), .Q(d_ff_1_q[6]));  // open: Qn, preset, reset
  D_Flip_Flop #(.trigger("high")) d_ff_8 (.D(D[7]), .clk(S), .Q(d_ff_1_q[7]));  // open: Qn, preset, reset
  LED led_1 (.in(d_ff_1_q[0]));
  LED led_2 (.in(d_ff_1_q[1]));
  LED led_3 (.in(d_ff_1_q[2]));
  LED led_4 (.in(d_ff_1_q[3]));
  LED led_5 (.in(d_ff_1_q[4]));
  LED led_6 (.in(d_ff_1_q[5]));
  LED led_7 (.in(d_ff_1_q[6]));
  LED led_8 (.in(d_ff_1_q[7]));
  assign O = E ? d_ff_1_q : 8'bz;  // Controlled_Buffer controlled_buffer_1
endmodule

module byte_reg_2 (
  input  [7:0] i,
  input  s,
  input  e,
  output [7:0] o
);

  wire [7:0] register_1_q;

  Register #(.trigger("high")) register_1 (.D(i), .en(s), .clk(s), .Q(register_1_q));  // open: clr
  assign o = e ? register_1_q : 8'bz;  // Controlled_Buffer controlled_buffer_1
endmodule

module decoder_3_8 (
  input  [2:0] in_1,
  output [7:0] out_2
);

  wire not_1_out, not_2_out, not_3_out;

  not not_1 (not_1_out, in_1[0]);
  not not_2 (not_2_out, in_1[1]);
  not not_3 (not_3_out, in_1[2]);
  and and_1 (out_2[0], not_3_out, not_2_out, not_1_out);
  and and_2 (out_2[1], not_3_out, not_2_out, in_1[0]);
  and and_3 (out_2[2], not_3_out, in_1[1], not_1_out);
  and and_4 (out_2[3], not_3_out, in_1[1], in_1[0]);
  and and_5 (out_2[4], in_1[2], not_2_out, not_1_out);
  and and_6 (out_2[5], in_1[2], not_2_out, in_1[0]);
  and and_7 (out_2[6], in_1[2], in_1[1], not_1_out);
  and and_8 (out_2[7], in_1[2], in_1[1], in_1[0]);
endmodule

module decoder_4_16 (
  input  [3:0] in_1,
  output [15:0] out_2
);

  wire not_1_out, not_2_out, not_3_out, not_4_out;

  not not_1 (not_1_out, in_1[0]);
  not not_2 (not_2_out, in_1[1]);
  not not_3 (not_3_out, in_1[2]);
  not not_4 (not_4_out, in_1[3]);
  and and_1 (out_2[0], not_4_out, not_3_out, not_2_out, not_1_out);
  and and_2 (out_2[1], not_4_out, not_3_out, not_2_out, in_1[0]);
  and and_3 (out_2[2], not_4_out, not_3_out, in_1[1], not_1_out);
  and and_4 (out_2[3], not_4_out, not_3_out, in_1[1], in_1[0]);
  and and_5 (out_2[4], not_4_out, in_1[2], not_2_out, not_1_out);
  and and_6 (out_2[5], not_4_out, in_1[2], not_2_out, in_1[0]);
  and and_7 (out_2[6], not_4_out, in_1[2], in_1[1], not_1_out);
  and and_8 (out_2[7], not_4_out, in_1[2], in_1[1], in_1[0]);
  and and_9 (out_2[8], in_1[3], not_3_out, not_2_out, not_1_out);
  and and_10 (out_2[9], in_1[3], not_3_out, not_2_out, in_1[0]);
  and and_11 (out_2[10], in_1[3], not_3_out, in_1[1], not_1_out);
  and and_12 (out_2[11], in_1[3], not_3_out, in_1[1], in_1[0]);
  and and_13 (out_2[12], in_1[3], in_1[2], not_2_out, not_1_out);
  and and_14 (out_2[13], in_1[3], in_1[2], not_2_out, in_1[0]);
  and and_15 (out_2[14], in_1[3], in_1[2], in_1[1], not_1_out);
  and and_16 (out_2[15], in_1[3], in_1[2], in_1[1], in_1[0]);
endmodule

module shift_l (
  input  [7:0] a,
  input  shft_i,
  output [7:0] b,
  output shft_o
);

  wire [6:0] byte_reg_2_1_o;

  byte_reg_2 byte_reg_2_1 (.o({shft_o, byte_reg_2_1_o}), .i(a), .e(1'b1), .s(1'b1));
  byte_reg_2 byte_reg_2_2 (.o(b), .i({byte_reg_2_1_o, shft_i}), .e(1'b1), .s(1'b1));
endmodule

module shift_l_2 (
  input  [7:0] a,
  input  shft_i,
  output [7:0] b,
  output shft_o
);

  wire not_1_out;
  wire [7:0] controlled_buffer_1_out, shifter_1_out;

  Shifter shifter_1 (.in(a), .\dist (3'b001), .out(shifter_1_out));
  not not_1 (not_1_out, shft_i);
  assign controlled_buffer_1_out = shft_i ? 8'h1 : 8'bz;  // Controlled_Buffer controlled_buffer_1
  assign controlled_buffer_1_out = not_1_out ? {8{1'b0}} : 8'bz;  // Controlled_Buffer controlled_buffer_2
  assign b = shifter_1_out | controlled_buffer_1_out;  // OR_Gate or_1, 8 bits wide
  BitSelector bitselector_1 (.in(a), .out(shft_o), .sel(3'b111));
endmodule

module shift_r (
  input  [7:0] a,
  input  shft_i,
  output [7:0] b,
  output shft_o
);

  wire [7:1] byte_reg_2_1_o;

  byte_reg_2 byte_reg_2_1 (.o({byte_reg_2_1_o, shft_o}), .i(a), .e(1'b1), .s(1'b1));
  byte_reg_2 byte_reg_2_2 (.o(b), .i({shft_i, byte_reg_2_1_o}), .e(1'b1), .s(1'b1));
endmodule

module shift_r_2 (
  input  [7:0] a,
  input  shft_i,
  output [7:0] b,
  output shft_o
);

  wire not_1_out;
  wire [7:0] controlled_buffer_1_out, shifter_1_out;

  Shifter #(.shift("lr")) shifter_1 (.in(a), .\dist (3'b001), .out(shifter_1_out));
  not not_1 (not_1_out, shft_i);
  assign controlled_buffer_1_out = shft_i ? 8'h80 : 8'bz;  // Controlled_Buffer controlled_buffer_1
  assign controlled_buffer_1_out = not_1_out ? {8{1'b0}} : 8'bz;  // Controlled_Buffer controlled_buffer_2
  assign b = shifter_1_out | controlled_buffer_1_out;  // OR_Gate or_1, 8 bits wide
  BitSelector bitselector_1 (.in(a), .out(shft_o), .sel(3'b000));
endmodule

module byte_not (
  input  [7:0] a,
  output [7:0] b
);

  not not_1 (b[7], a[7]);
  not not_2 (b[6], a[6]);
  not not_3 (b[5], a[5]);
  not not_4 (b[4], a[4]);
  not not_5 (b[3], a[3]);
  not not_6 (b[2], a[2]);
  not not_7 (b[1], a[1]);
  not not_8 (b[0], a[0]);
endmodule

module byte_and (
  input  [7:0] a,
  input  [7:0] b,
  output [7:0] c
);

  and and_1 (c[7], a[7], b[7]);
  and and_2 (c[6], a[6], b[6]);
  and and_3 (c[5], a[5], b[5]);
  and and_4 (c[4], a[4], b[4]);
  and and_5 (c[3], a[3], b[3]);
  and and_6 (c[2], a[2], b[2]);
  and and_7 (c[1], a[1], b[1]);
  and and_8 (c[0], a[0], b[0]);
endmodule

module byte_or (
  input  [7:0] a,
  input  [7:0] b,
  output [7:0] c
);

  or or_1 (c[7], a[7], b[7]);
  or or_2 (c[6], a[6], b[6]);
  or or_3 (c[5], a[5], b[5]);
  or or_4 (c[4], a[4], b[4]);
  or or_5 (c[3], a[3], b[3]);
  or or_6 (c[2], a[2], b[2]);
  or or_7 (c[1], a[1], b[1]);
  or or_8 (c[0], a[0], b[0]);
endmodule

module byte_xor (
  input  [7:0] a,
  input  [7:0] b,
  output [7:0] c
);

  xor xor_1 (c[7], a[7], b[7]);
  xor xor_2 (c[6], a[6], b[6]);
  xor xor_3 (c[5], a[5], b[5]);
  xor xor_4 (c[4], a[4], b[4]);
  xor xor_5 (c[3], a[3], b[3]);
  xor xor_6 (c[2], a[2], b[2]);
  xor xor_7 (c[1], a[1], b[1]);
  xor xor_8 (c[0], a[0], b[0]);
endmodule

module bit_adder (
  input  a,
  input  b,
  input  c_in,
  output s,
  output c_out
);

  wire and_1_out, and_2_out, xor_1_out;

  xor xor_1 (xor_1_out, a, b);
  and and_1 (and_1_out, c_in, xor_1_out);
  and and_2 (and_2_out, a, b);
  xor xor_2 (s, xor_1_out, c_in);
  or or_1 (c_out, and_1_out, and_2_out);
endmodule

module byte_adder (
  input  [7:0] a,
  input  [7:0] b,
  input  c_in,
  output [7:0] s,
  output c_out
);

  wire bit_adder_2_c_out, bit_adder_3_c_out, bit_adder_4_c_out, bit_adder_5_c_out, bit_adder_6_c_out,
       bit_adder_7_c_out, bit_adder_8_c_out;

  bit_adder bit_adder_1 (.a(a[7]), .b(b[7]), .c_in(bit_adder_2_c_out), .s(s[7]), .c_out(c_out));
  bit_adder bit_adder_2 (.a(a[6]), .b(b[6]), .c_in(bit_adder_3_c_out), .s(s[6]), .c_out(bit_adder_2_c_out));
  bit_adder bit_adder_3 (.a(a[5]), .b(b[5]), .c_in(bit_adder_4_c_out), .s(s[5]), .c_out(bit_adder_3_c_out));
  bit_adder bit_adder_4 (.a(a[4]), .b(b[4]), .c_in(bit_adder_5_c_out), .s(s[4]), .c_out(bit_adder_4_c_out));
  bit_adder bit_adder_5 (.a(a[3]), .b(b[3]), .c_in(bit_adder_6_c_out), .s(s[3]), .c_out(bit_adder_5_c_out));
  bit_adder bit_adder_6 (.a(a[2]), .b(b[2]), .c_in(bit_adder_7_c_out), .s(s[2]), .c_out(bit_adder_6_c_out));
  bit_adder bit_adder_7 (.a(a[1]), .b(b[1]), .c_in(bit_adder_8_c_out), .s(s[1]), .c_out(bit_adder_7_c_out));
  bit_adder bit_adder_8 (.a(a[0]), .b(b[0]), .c_in(c_in), .s(s[0]), .c_out(bit_adder_8_c_out));
endmodule

module bit_cmp (
  input  a,
  input  b,
  input  equ_in,
  input  gtr_in,
  output c,
  output equ_out,
  output gtr_out
);

  wire and_2_out, not_1_out;

  xor xor_1 (c, a, b);
  not not_1 (not_1_out, c);
  and and_1 (equ_out, not_1_out, equ_in);
  and and_2 (and_2_out, equ_in, a, c);
  or or_1 (gtr_out, and_2_out, gtr_in);
endmodule

module byte_cmp (
  input  [7:0] a,
  input  [7:0] b,
  output [7:0] c,
  output equ_out,
  output gtr_a_out
);

  wire bit_cmp_1_equ_out, bit_cmp_1_gtr_out, bit_cmp_2_equ_out, bit_cmp_2_gtr_out, bit_cmp_3_equ_out,
       bit_cmp_3_gtr_out, bit_cmp_4_equ_out, bit_cmp_4_gtr_out, bit_cmp_5_equ_out, bit_cmp_5_gtr_out,
       bit_cmp_6_equ_out, bit_cmp_6_gtr_out, bit_cmp_7_equ_out, bit_cmp_7_gtr_out;

  bit_cmp bit_cmp_1 (
    .a(a[7]), .b(b[7]), .equ_in(1'b1), .gtr_in(1'b0), .c(c[7]), .equ_out(bit_cmp_1_equ_out),
    .gtr_out(bit_cmp_1_gtr_out));
  bit_cmp bit_cmp_2 (
    .a(a[6]), .b(b[6]), .equ_in(bit_cmp_1_equ_out), .gtr_in(bit_cmp_1_gtr_out), .c(c[6]),
    .equ_out(bit_cmp_2_equ_out), .gtr_out(bit_cmp_2_gtr_out));
  bit_cmp bit_cmp_3 (
    .a(a[5]), .b(b[5]), .equ_in(bit_cmp_2_equ_out), .gtr_in(bit_cmp_2_gtr_out), .c(c[5]),
    .equ_out(bit_cmp_3_equ_out), .gtr_out(bit_cmp_3_gtr_out));
  bit_cmp bit_cmp_4 (
    .a(a[4]), .b(b[4]), .equ_in(bit_cmp_3_equ_out), .gtr_in(bit_cmp_3_gtr_out), .c(c[4]),
    .equ_out(bit_cmp_4_equ_out), .gtr_out(bit_cmp_4_gtr_out));
  bit_cmp bit_cmp_5 (
    .a(a[3]), .b(b[3]), .equ_in(bit_cmp_4_equ_out), .gtr_in(bit_cmp_4_gtr_out), .c(c[3]),
    .equ_out(bit_cmp_5_equ_out), .gtr_out(bit_cmp_5_gtr_out));
  bit_cmp bit_cmp_6 (
    .a(a[2]), .b(b[2]), .equ_in(bit_cmp_5_equ_out), .gtr_in(bit_cmp_5_gtr_out), .c(c[2]),
    .equ_out(bit_cmp_6_equ_out), .gtr_out(bit_cmp_6_gtr_out));
  bit_cmp bit_cmp_7 (
    .a(a[1]), .b(b[1]), .equ_in(bit_cmp_6_equ_out), .gtr_in(bit_cmp_6_gtr_out), .c(c[1]),
    .equ_out(bit_cmp_7_equ_out), .gtr_out(bit_cmp_7_gtr_out));
  bit_cmp bit_cmp_8 (
    .a(a[0]), .b(b[0]), .equ_in(bit_cmp_7_equ_out), .gtr_in(bit_cmp_7_gtr_out), .c(c[0]), .equ_out(equ_out),
    .gtr_out(gtr_a_out));
endmodule

module byte_zero_check (
  input  [7:0] bus_in,
  output out_2
);

  nor nor_1 (out_2, bus_in[7], bus_in[6], bus_in[5], bus_in[4], bus_in[3], bus_in[2], bus_in[1], bus_in[0]);
endmodule

module clk_src (
  output clk,
  output clk_d,
  output clk_s,
  output clk_e
);

  Clock #(.highDuration(2), .lowDuration(2)) clk_1 (.out(clk));
  Clock #(.highDuration(2), .lowDuration(2), .phaseOffset(3)) clk_2 (.out(clk_d));
  and and_1 (clk_s, clk, clk_d);
  or or_1 (clk_e, clk, clk_d);
endmodule

module stepper (
  input  clk,
  output s_1,
  output s_2,
  output s_3,
  output s_4,
  output s_5,
  output s_6
);

  wire d_ff_1_q, d_ff_2_q, d_ff_3_q, d_ff_4_q, d_ff_5_q, d_ff_6_q, d_ff_7_q, d_ff_8_q, d_ff_9_q, d_ff_10_q,
       d_ff_11_q, d_ff_12_q, not_1_out, not_2_out, not_3_out, not_4_out, not_5_out, not_6_out, not_7_out,
       or_1_out, or_2_out;

  or or_1 (or_1_out, d_ff_12_q, not_1_out);
  not not_1 (not_1_out, clk);
  or or_2 (or_2_out, d_ff_12_q, clk);
  D_Flip_Flop d_ff_1 (.D(1'b1), .clk(or_1_out), .Q(d_ff_1_q), .reset(d_ff_12_q));  // open: Qn, preset
  or or_3 (s_1, d_ff_12_q, not_2_out);
  not not_2 (not_2_out, d_ff_2_q);
  D_Flip_Flop d_ff_2 (.D(d_ff_1_q), .clk(or_2_out), .Q(d_ff_2_q), .reset(d_ff_12_q));  // open: Qn, preset
  D_Flip_Flop d_ff_3 (.D(d_ff_2_q), .clk(or_1_out), .Q(d_ff_3_q), .reset(d_ff_12_q));  // open: Qn, preset
  and and_1 (s_2, d_ff_2_q, not_3_out);
  not not_3 (not_3_out, d_ff_4_q);
  D_Flip_Flop d_ff_4 (.D(d_ff_3_q), .clk(or_2_out), .Q(d_ff_4_q), .reset(d_ff_12_q));  // open: Qn, preset
  not not_4 (not_4_out, d_ff_6_q);
  D_Flip_Flop d_ff_5 (.D(d_ff_4_q), .clk(or_1_out), .Q(d_ff_5_q), .reset(d_ff_12_q));  // open: Qn, preset
  and and_2 (s_3, d_ff_4_q, not_4_out);
  D_Flip_Flop d_ff_6 (.D(d_ff_5_q), .clk(or_2_out), .Q(d_ff_6_q), .reset(d_ff_12_q));  // open: Qn, preset
  not not_5 (not_5_out, d_ff_8_q);
  D_Flip_Flop d_ff_7 (.D(d_ff_6_q), .clk(or_1_out), .Q(d_ff_7_q), .reset(d_ff_12_q));  // open: Qn, preset
  and and_3 (s_4, d_ff_6_q, not_5_out);
  D_Flip_Flop d_ff_8 (.D(d_ff_7_q), .clk(or_2_out), .Q(d_ff_8_q), .reset(d_ff_12_q));  // open: Qn, preset
  D_Flip_Flop d_ff_9 (.D(d_ff_8_q), .clk(or_1_out), .Q(d_ff_9_q), .reset(d_ff_12_q));  // open: Qn, preset
  and and_4 (s_5, d_ff_8_q, not_6_out);
  not not_6 (not_6_out, d_ff_10_q);
  D_Flip_Flop d_ff_10 (.D(d_ff_9_q), .clk(or_2_out), .Q(d_ff_10_q), .reset(d_ff_12_q));  // open: Qn, preset
  D_Flip_Flop d_ff_11 (.D(d_ff_10_q), .clk(or_1_out), .Q(d_ff_11_q), .reset(d_ff_12_q));  // open: Qn, preset
  and and_5 (s_6, d_ff_10_q, not_7_out);
  not not_7 (not_7_out, d_ff_12_q);
  D_Flip_Flop d_ff_12 (.D(d_ff_11_q), .clk(or_2_out), .Q(d_ff_12_q), .reset(d_ff_12_q));  // open: Qn, preset
endmodule

module alu (
  input  [7:0] a,
  input  [7:0] b,
  input  carry_in,
  input  [2:0] opcode,
  output equ,
  output gtr_a,
  output zero,
  output [7:0] c,
  output carry_out
);

  wire and_1_out, and_2_out, and_3_out, byte_adder_1_c_out, shift_l_1_shft_o, shift_r_1_shft_o;
  wire [7:0] byte_adder_1_s, byte_and_1_c, byte_cmp_1_c, byte_not_1_b, byte_or_1_c, decoder_3_8_1_out_2,
       shift_l_1_b, shift_r_1_b;

  byte_cmp byte_cmp_1 (.a(a), .b(b), .c(byte_cmp_1_c), .equ_out(equ), .gtr_a_out(gtr_a));
  byte_or byte_or_1 (.a(a), .b(b), .c(byte_or_1_c));
  byte_and byte_and_1 (.a(a), .b(b), .c(byte_and_1_c));
  byte_not byte_not_1 (.a(a), .b(byte_not_1_b));
  shift_l shift_l_1 (.a(a), .shft_i(carry_in), .b(shift_l_1_b), .shft_o(shift_l_1_shft_o));
  shift_r shift_r_1 (.a(a), .shft_i(carry_in), .b(shift_r_1_b), .shft_o(shift_r_1_shft_o));
  byte_adder byte_adder_1 (.a(a), .b(b), .c_in(carry_in), .s(byte_adder_1_s), .c_out(byte_adder_1_c_out));
  decoder_3_8 decoder_3_8_1 (.in_1(opcode), .out_2(decoder_3_8_1_out_2));
  and and_1 (and_1_out, shift_l_1_shft_o, decoder_3_8_1_out_2[2]);
  and and_2 (and_2_out, shift_r_1_shft_o, decoder_3_8_1_out_2[1]);
  and and_3 (and_3_out, byte_adder_1_c_out, decoder_3_8_1_out_2[0]);
  enabler enabler_1 (.i(byte_cmp_1_c), .e(decoder_3_8_1_out_2[6]), .o(c));
  enabler enabler_2 (.i(byte_or_1_c), .e(decoder_3_8_1_out_2[5]), .o(c));
  enabler enabler_3 (.i(byte_and_1_c), .e(decoder_3_8_1_out_2[4]), .o(c));
  enabler enabler_4 (.i(byte_not_1_b), .e(decoder_3_8_1_out_2[3]), .o(c));
  enabler enabler_5 (.i(shift_l_1_b), .e(decoder_3_8_1_out_2[2]), .o(c));
  enabler enabler_6 (.i(shift_r_1_b), .e(decoder_3_8_1_out_2[1]), .o(c));
  enabler enabler_7 (.i(byte_adder_1_s), .e(decoder_3_8_1_out_2[0]), .o(c));
  or or_1 (carry_out, and_1_out, and_2_out, and_3_out);
  byte_zero_check byte_zero_check_1 (.out_2(zero));  // open: bus_in
endmodule

module alu2 (
  input  [7:0] a,
  input  [7:0] b,
  input  [2:0] opcode,
  input  carry_in,
  output [7:0] c,
  output gtr_a,
  output equ,
  output zero,
  output carry_out
);

  wire adder_1_cout, and_2_out, and_3_out, and_4_out, decoder_1_out0, decoder_1_out1, decoder_1_out2,
       decoder_1_out3, decoder_1_out4, decoder_1_out5, decoder_1_out6, shift_l_2_1_shft_o, shift_r_2_1_shft_o;
  wire [7:0] adder_1_out, and_1_out, not_1_out, or_1_out, shift_l_2_1_b, shift_r_2_1_b, xor_1_out;

  Comparator comparator_1 (.a(a), .b(b), .gt(gtr_a), .eq(equ));  // open: lt
  assign and_1_out = a & b;  // AND_Gate and_1, 8 bits wide
  assign not_1_out = ~a;  // NOT_Gate not_1, 8 bits wide
  Adder adder_1 (.a(a), .b(b), .out(adder_1_out), .cin(carry_in), .cout(adder_1_cout));
  assign xor_1_out = a ^ b;  // XOR_Gate xor_1, 8 bits wide
  assign or_1_out = a | b;  // OR_Gate or_1, 8 bits wide
  shift_l_2 shift_l_2_1 (.a(a), .shft_i(carry_in), .b(shift_l_2_1_b), .shft_o(shift_l_2_1_shft_o));
  shift_r_2 shift_r_2_1 (.a(a), .shft_i(carry_in), .b(shift_r_2_1_b), .shft_o(shift_r_2_1_shft_o));
  Decoder #(.select(3)) decoder_1 (
    .out0(decoder_1_out0), .out1(decoder_1_out1), .out2(decoder_1_out2), .out3(decoder_1_out3),
    .out4(decoder_1_out4), .out5(decoder_1_out5), .out6(decoder_1_out6), .sel(opcode));  // open: out7, en
  assign c = decoder_1_out6 ? xor_1_out : 8'bz;  // Controlled_Buffer controlled_buffer_1
  assign c = decoder_1_out5 ? or_1_out : 8'bz;  // Controlled_Buffer controlled_buffer_2
  assign c = decoder_1_out4 ? and_1_out : 8'bz;  // Controlled_Buffer controlled_buffer_3
  assign c = decoder_1_out3 ? not_1_out : 8'bz;  // Controlled_Buffer controlled_buffer_4
  assign c = decoder_1_out2 ? shift_l_2_1_b : 8'bz;  // Controlled_Buffer controlled_buffer_5
  assign c = decoder_1_out1 ? shift_r_2_1_b : 8'bz;  // Controlled_Buffer controlled_buffer_6
  assign c = decoder_1_out0 ? adder_1_out : 8'bz;  // Controlled_Buffer controlled_buffer_7
  and and_2 (and_2_out, shift_l_2_1_shft_o, decoder_1_out2);
  and and_3 (and_3_out, shift_r_2_1_shft_o, decoder_1_out1);
  and and_4 (and_4_out, adder_1_cout, decoder_1_out0);
  or or_2 (carry_out, and_2_out, and_3_out, and_4_out);
  byte_zero_check byte_zero_check_1 (.bus_in(c), .out_2(zero));

  // Notes on the sheet:
  //   000 ADD, 001 SHR, 010 SHL, 011 NOT, 100 AND, 101 OR, 110 XOR, 111 CMP
endmodule

module bus_1 (
  input  [7:0] i,
  input  e,
  output [7:0] o
);

  wire not_1_out;

  not not_1 (not_1_out, e);
  or or_1 (o[0], e, i[0]);
  and and_1 (o[1], not_1_out, i[1]);
  and and_2 (o[2], not_1_out, i[2]);
  and and_3 (o[3], not_1_out, i[3]);
  and and_4 (o[4], not_1_out, i[4]);
  and and_5 (o[5], not_1_out, i[5]);
  and and_6 (o[6], not_1_out, i[6]);
  and and_7 (o[7], not_1_out, i[7]);
endmodule

module bus_1_2 (
  input  [7:0] i,
  input  e,
  output [7:0] o
);

  wire not_1_out;

  assign o = not_1_out ? i : 8'bz;  // Controlled_Buffer controlled_buffer_1
  not not_1 (not_1_out, e);
  assign o = e ? 8'h1 : 8'bz;  // Controlled_Buffer controlled_buffer_2
endmodule

module cpu (
);

  wire ACC_EN, ACC_SET, BUS1_EN, carry_en, control_unit_1_carry_en, control_unit_1_flag_set, IAR_EN, IAR_SET,
       IR_SET, MAR_SET, R0_EN, R0_SET, R1_EN, R1_SET, R2_EN, R2_SET, R3_EN, R3_SET, RAM_EN, RAM_SET, TMP_SET,
       undriven;
  wire [2:0] OPCODE;
  wire [7:0] alu2_1_c, alu2_1_zero, bus_1_2_1_o, byte_reg_2_1_o, byte_reg_2_2_o, byte_reg_2_4_o,
       byte_reg_2_6_o, byte_reg_2_10_o;

  byte_reg_2 byte_reg_2_1 (.o(byte_reg_2_1_o), .i(byte_reg_2_2_o), .e(1'b1), .s(TMP_SET));
  bus_1_2 bus_1_2_1 (.o(bus_1_2_1_o), .i(byte_reg_2_1_o), .e(BUS1_EN));
  alu2 alu2_1 (
    .c(alu2_1_c), .carry_out(alu2_1_zero[3]), .gtr_a(alu2_1_zero[2]), .equ(alu2_1_zero[1]),
    .zero(alu2_1_zero[0]), .a(byte_reg_2_2_o), .b(bus_1_2_1_o), .opcode(OPCODE), .carry_in(carry_en));
  byte_reg_2 byte_reg_2_2 (.o(byte_reg_2_2_o), .i(alu2_1_c), .e(ACC_EN), .s(ACC_SET));
  byte_reg_2 byte_reg_2_3 (.o(byte_reg_2_2_o), .i(byte_reg_2_2_o), .e(R0_EN), .s(R0_SET));
  and and_1 (carry_en, control_unit_1_carry_en, undriven);
  D_Flip_Flop #(.trigger("high")) d_ff_1 (
    .D(undriven), .clk(TMP_SET), .Q(byte_reg_2_4_o[3]));  // open: Qn, preset, reset
  byte_reg_2 byte_reg_2_4 (.o(byte_reg_2_4_o), .i(alu2_1_zero), .e(1'b1), .s(control_unit_1_flag_set));
  byte_reg_2 byte_reg_2_5 (.o(byte_reg_2_2_o), .i(byte_reg_2_2_o), .e(R1_EN), .s(R1_SET));
  byte_reg_2 byte_reg_2_6 (.o(byte_reg_2_6_o), .i(byte_reg_2_2_o), .e(1'b1), .s(IR_SET));
  byte_reg_2 byte_reg_2_7 (.o(byte_reg_2_2_o), .i(byte_reg_2_2_o), .e(R2_EN), .s(R2_SET));
  control_unit control_unit_1 (
    .OP_OUT(OPCODE), .BUS1_EN(BUS1_EN), .CARRY_EN(control_unit_1_carry_en), .R0_EN(R0_EN), .R1_EN(R1_EN),
    .R2_EN(R2_EN), .R3_EN(R3_EN), .RAM_EN(RAM_EN), .IAR_EN(IAR_EN), .ACC_EN(ACC_EN), .TMP_SET(TMP_SET),
    .FLAG_SET(control_unit_1_flag_set), .R0_SET(R0_SET), .R1_SET(R1_SET), .R2_SET(R2_SET), .R3_SET(R3_SET),
    .MAR_SET(MAR_SET), .RAM_SET(RAM_SET), .IAR_SET(IAR_SET), .IR_SET(IR_SET), .ACC_SET(ACC_SET),
    .IR_IN(byte_reg_2_6_o), .FLAG_C(byte_reg_2_4_o[3]), .FLAG_A(byte_reg_2_4_o[0]),
    .FLAG_E(byte_reg_2_4_o[1]), .FLAG_Z(byte_reg_2_4_o[2]));
  byte_reg_2 byte_reg_2_8 (.o(byte_reg_2_2_o), .i(byte_reg_2_2_o), .e(IAR_EN), .s(IAR_SET));
  byte_reg_2 byte_reg_2_9 (.o(byte_reg_2_2_o), .i(byte_reg_2_2_o), .e(R3_EN), .s(R3_SET));
  RAM #(.databus("bidir"), .trigger("high")) ram_1 (
    .addr(byte_reg_2_10_o), .we(RAM_SET), .oe(RAM_EN), .data(byte_reg_2_2_o));
  byte_reg_2 byte_reg_2_10 (.o(byte_reg_2_10_o), .i(byte_reg_2_2_o), .e(1'b1), .s(MAR_SET));
endmodule

module control_unit (
  input  [7:0] IR_IN,
  input  FLAG_C,
  input  FLAG_A,
  input  FLAG_E,
  input  FLAG_Z,
  output MAR_SET,
  output RAM_EN,
  output RAM_SET,
  output IAR_EN,
  output IAR_SET,
  output IR_SET,
  output ACC_EN,
  output ACC_SET,
  output BUS1_EN,
  output TMP_SET,
  output CARRY_EN,
  output FLAG_SET,
  output R0_EN,
  output R0_SET,
  output R1_EN,
  output R1_SET,
  output [2:0] OP_OUT,
  output R2_EN,
  output R2_SET,
  output R3_EN,
  output R3_SET
);

  wire and_26_out, and_27_out, and_28_out, and_29_out, and_30_out, and_31_out, and_32_out, and_33_out,
       and_49_out, and_50_out, and_51_out, and_52_out, clk_e, clk_s, clk_src_1_clk, CU_ACC_EN_1, CU_ACC_EN_2,
       CU_ACC_EN_3, CU_ACC_EN_4, CU_ACC_SET_1, CU_ACC_SET_2, CU_ACC_SET_3, CU_ACC_SET_4, CU_BUS1_EN_4,
       CU_CLF_CMD, CU_DATA_CMD, CU_IAR_EN_3, CU_IAR_SET_3, CU_IAR_SET_4, CU_IAR_SET_5, CU_IR_SET_1,
       CU_JMP_CMD, CU_JMPR_CMD, CU_JXX_CMD, CU_LD_CMD, CU_MAR_SET_2, CU_MAR_SET_3, CU_R0_EN_1, CU_R0_SET_1,
       CU_R1_EN_1, CU_R1_SET_1, CU_R2_EN_1, CU_R2_SET_1, CU_R3_EN_1, CU_R3_SET_1, CU_RAM_EN_2, CU_RAM_EN_3,
       CU_RAM_SET_1, CU_REG_A_EN_1, CU_ST_CMD, decoder_1_out0, decoder_1_out1, decoder_1_out2,
       decoder_1_out3, decoder_2_out0, decoder_2_out1, decoder_2_out2, decoder_2_out3, decoder_3_out0,
       decoder_3_out1, decoder_3_out2, decoder_3_out3, decoder_4_out0, decoder_4_out1, decoder_4_out2,
       decoder_4_out3, decoder_4_out4, decoder_4_out5, decoder_4_out6, decoder_4_out7, nand_1_out, not_1_out,
       or_1_out, or_2_out, or_3_out, or_4_out, or_5_out, or_6_out, or_7_out, or_8_out, or_9_out, or_10_out,
       or_11_out, or_16_out, or_17_out, or_18_out, or_19_out, STEP_4, STEP_5, STEP_6;

  and and_1 (RAM_EN, clk_e, or_1_out);
  and and_2 (IAR_EN, clk_e, or_2_out);
  and and_3 (ACC_EN, clk_e, or_3_out);
  and and_4 (BUS1_EN, clk_e, or_4_out);
  and and_5 (CARRY_EN, clk_e, CU_ACC_SET_2);
  and and_6 (R0_EN, clk_e, CU_R0_EN_1);
  and and_7 (R1_EN, clk_e, CU_R1_EN_1);
  and and_8 (R2_EN, clk_e, CU_R2_EN_1);
  and and_9 (R3_EN, clk_e, CU_R3_EN_1);
  clk_src clk_src_1 (.clk(clk_src_1_clk), .clk_s(clk_s), .clk_e(clk_e));  // open: clk_d
  or or_1 (or_1_out, CU_IR_SET_1, CU_RAM_EN_2, CU_RAM_EN_3, CU_IAR_SET_4, CU_IAR_SET_5);
  or or_2 (or_2_out, CU_ACC_SET_1, CU_ACC_SET_3, CU_IAR_EN_3, CU_ACC_SET_4);
  or or_3 (or_3_out, CU_ACC_EN_1, CU_ACC_EN_2, CU_ACC_EN_3, CU_ACC_EN_4);
  or or_4 (or_4_out, CU_ACC_SET_1, CU_ACC_SET_3, CU_ACC_SET_4, CU_BUS1_EN_4);
  stepper stepper_1 (
    .s_4(STEP_4), .s_5(STEP_5), .s_6(STEP_6), .s_1(CU_ACC_SET_1), .s_2(CU_IR_SET_1), .s_3(CU_ACC_EN_1),
    .clk(clk_src_1_clk));
  LED led_1 (.in(CU_ACC_SET_1));
  LED led_2 (.in(CU_IR_SET_1));
  LED led_3 (.in(CU_ACC_EN_1));
  LED led_4 (.in(STEP_4));
  LED led_5 (.in(STEP_5));
  LED led_6 (.in(STEP_6));
  or or_5 (or_5_out, CU_ACC_SET_1, CU_MAR_SET_2, CU_MAR_SET_3, CU_ACC_SET_3, CU_IAR_EN_3, CU_ACC_SET_4);
  or or_6 (or_6_out, CU_RAM_SET_1, CU_RAM_SET_1);
  or or_7 (or_7_out, CU_ACC_EN_1, CU_ACC_EN_3, CU_IAR_SET_3, CU_IAR_SET_4, CU_IAR_SET_5, CU_ACC_EN_4);
  buf or_8 (or_8_out, CU_IR_SET_1);  // OR_Gate
  or or_9 (or_9_out, CU_ACC_SET_1, CU_ACC_SET_2, CU_ACC_SET_3, CU_ACC_SET_4);
  buf or_10 (or_10_out, CU_REG_A_EN_1);  // OR_Gate
  or or_11 (or_11_out, CU_ACC_SET_2, CU_BUS1_EN_4);
  and and_10 (MAR_SET, clk_s, or_5_out);
  and and_11 (RAM_SET, clk_s, or_6_out);
  and and_12 (IAR_SET, clk_s, or_7_out);
  and and_13 (IR_SET, clk_s, or_8_out);
  and and_14 (ACC_SET, clk_s, or_9_out);
  and and_15 (TMP_SET, clk_s, or_10_out);
  and and_16 (FLAG_SET, clk_s, or_11_out);
  and and_17 (R0_SET, clk_s, CU_R0_SET_1);
  and and_18 (R1_SET, clk_s, CU_R1_SET_1);
  and and_19 (R2_SET, clk_s, CU_R2_SET_1);
  and and_20 (R3_SET, clk_s, CU_R3_SET_1);
  or or_12 (CU_R0_EN_1, and_26_out, and_30_out);
  or or_13 (CU_R1_EN_1, and_27_out, and_31_out);
  or or_14 (CU_R2_EN_1, and_28_out, and_32_out);
  or or_15 (CU_R3_EN_1, and_29_out, and_33_out);
  and and_21 (CU_MAR_SET_2, STEP_4, CU_LD_CMD);
  and and_22 (CU_RAM_EN_2, STEP_4, CU_ST_CMD);
  and and_23 (CU_IAR_SET_3, STEP_4, CU_JMPR_CMD);
  and and_24 (CU_IAR_EN_3, STEP_4, CU_JMP_CMD);
  and and_25 (CU_BUS1_EN_4, STEP_4, CU_CLF_CMD);
  or or_16 (or_16_out, CU_REG_A_EN_1, CU_MAR_SET_2, CU_MAR_SET_3);
  or or_17 (or_17_out, CU_ACC_SET_2, CU_RAM_SET_1, CU_IAR_SET_3);
  and and_26 (and_26_out, clk_e, or_17_out, decoder_1_out0);
  and and_27 (and_27_out, clk_e, or_17_out, decoder_1_out1);
  and and_28 (and_28_out, clk_e, or_17_out, decoder_1_out2);
  and and_29 (and_29_out, clk_e, or_17_out, decoder_1_out3);
  and and_30 (and_30_out, clk_e, or_16_out, decoder_3_out0);
  and and_31 (and_31_out, clk_e, or_16_out, decoder_3_out1);
  and and_32 (and_32_out, clk_e, or_16_out, decoder_3_out2);
  and and_33 (and_33_out, clk_e, or_16_out, decoder_3_out3);
  and and_34 (OP_OUT[0], STEP_5, IR_IN[7], IR_IN[4]);
  and and_35 (OP_OUT[1], STEP_5, IR_IN[7], IR_IN[5]);
  and and_36 (OP_OUT[2], STEP_5, IR_IN[7], IR_IN[6]);
  and and_37 (CU_MAR_SET_3, STEP_5, CU_LD_CMD);
  and and_38 (CU_RAM_SET_1, STEP_5, CU_ST_CMD);
  and and_39 (CU_IAR_SET_4, STEP_5, CU_JMP_CMD);
  and and_40 (CU_REG_A_EN_1, STEP_4, IR_IN[7]);
  Decoder #(.select(2)) decoder_1 (
    .out0(decoder_1_out0), .out1(decoder_1_out1), .out2(decoder_1_out2), .out3(decoder_1_out3),
    .sel(IR_IN[1:0]));  // open: en
  Decoder #(.select(2)) decoder_2 (
    .out0(decoder_2_out0), .out1(decoder_2_out1), .out2(decoder_2_out2), .out3(decoder_2_out3),
    .sel(IR_IN[1:0]));  // open: en
  Decoder #(.select(2)) decoder_3 (
    .out0(decoder_3_out0), .out1(decoder_3_out1), .out2(decoder_3_out2), .out3(decoder_3_out3),
    .sel(IR_IN[3:2]));  // open: en
  and and_41 (CU_ACC_SET_2, STEP_5, IR_IN[7]);
  or or_18 (or_18_out, CU_ACC_EN_2, CU_RAM_EN_2, CU_RAM_EN_3);
  and and_42 (CU_ACC_EN_2, STEP_6, IR_IN[7], nand_1_out);
  nand nand_1 (nand_1_out, IR_IN[4], IR_IN[5], IR_IN[6]);
  not not_1 (not_1_out, IR_IN[7]);
  Decoder #(.select(3)) decoder_4 (
    .out0(decoder_4_out0), .out1(decoder_4_out1), .out2(decoder_4_out2), .out3(decoder_4_out3),
    .out4(decoder_4_out4), .out5(decoder_4_out5), .out6(decoder_4_out6), .out7(decoder_4_out7),
    .sel(IR_IN[6:4]));  // open: en
  and and_43 (CU_R0_SET_1, clk_s, or_18_out, decoder_2_out0);
  and and_44 (CU_R1_SET_1, clk_s, or_18_out, decoder_2_out1);
  and and_45 (CU_R2_SET_1, clk_s, or_18_out, decoder_2_out2);
  and and_46 (CU_R3_SET_1, clk_s, or_18_out, decoder_2_out3);
  and and_47 (CU_ACC_SET_3, STEP_4, CU_DATA_CMD);
  and and_48 (CU_ACC_SET_4, STEP_4, CU_JXX_CMD);
  and and_49 (and_49_out, FLAG_C, IR_IN[3]);
  and and_50 (and_50_out, FLAG_A, IR_IN[2]);
  and and_51 (and_51_out, FLAG_E, IR_IN[1]);
  and and_52 (and_52_out, FLAG_Z, IR_IN[0]);
  and and_53 (CU_LD_CMD, not_1_out, decoder_4_out0);
  and and_54 (CU_ST_CMD, not_1_out, decoder_4_out1);
  and and_55 (CU_DATA_CMD, not_1_out, decoder_4_out2);
  and and_56 (CU_JMPR_CMD, not_1_out, decoder_4_out3);
  and and_57 (CU_JMP_CMD, not_1_out, decoder_4_out4);
  and and_58 (CU_JXX_CMD, not_1_out, decoder_4_out5);
  and and_59 (CU_CLF_CMD, not_1_out, decoder_4_out6);
  // AND_Gate and_60 has open pins: in0=not_1_out, in1=decoder_4_out7, out=open
  and and_61 (CU_RAM_EN_3, STEP_5, CU_DATA_CMD);
  and and_62 (CU_ACC_EN_4, STEP_5, CU_JXX_CMD);
  or or_19 (or_19_out, and_49_out, and_50_out, and_51_out, and_52_out);
  and and_63 (CU_ACC_EN_3, STEP_6, CU_DATA_CMD);
  and and_64 (CU_IAR_SET_5, STEP_6, CU_JXX_CMD, or_19_out);

  // Other names for the same wires on the sheet: CU_FLAG_SET_2 = CU_BUS1_EN_4; CU_IAR_SET_2 = CU_ACC_EN_3;
  //   CU_IAR_SET_6 = CU_ACC_EN_4; CU_BUS1_EN_2 = CU_ACC_SET_3; CU_IAR_EN_2 = CU_ACC_SET_3;
  //   CU_MAR_SET_4 = CU_ACC_SET_3; CU_MAR_SET_5 = CU_IAR_EN_3; CU_BUS1_EN_3 = CU_ACC_SET_4;
  //   CU_IAR_EN_4 = CU_ACC_SET_4; CU_MAR_SET_6 = CU_ACC_SET_4; CU_OPCODE[2:0] = IR_IN[6:4];
  //   CU_RAM_EN_4 = CU_IAR_SET_4; CU_RAM_EN_5 = CU_IAR_SET_5; CU_FLAG[3:0] = IR_IN[3:0]; CU_REG_A[1:0] = IR_IN[3:2];
  //   CU_REG_A_EN_2 = CU_MAR_SET_2; CU_REG_A_EN_3 = CU_MAR_SET_3; CU_REG_B[1:0] = IR_IN[1:0];
  //   CU_CARRY_EN = CU_ACC_SET_2; CU_FLAG_SET_1 = CU_ACC_SET_2; CU_REG_B_EN_1 = CU_ACC_SET_2;
  //   CU_REG_B_EN_2 = CU_RAM_SET_1; CU_REG_B_EN_3 = CU_IAR_SET_3; CU_REG_B_SET_1 = CU_ACC_EN_2;
  //   CU_REG_B_SET_2 = CU_RAM_EN_2; CU_REG_B_SET_3 = CU_RAM_EN_3; CU_TMP_SET_1 = CU_REG_A_EN_1; CU_ALU_EN = IR_IN[7];
  //   CU_BUS1_EN_1 = CU_ACC_SET_1; CU_IAR_EN_1 = CU_ACC_SET_1; CU_MAR_SET_1 = CU_ACC_SET_1; STEP_1 = CU_ACC_SET_1;
  //   CU_RAM_EN_1 = CU_IR_SET_1; STEP_2 = CU_IR_SET_1; CU_IAR_SET_1 = CU_ACC_EN_1; STEP_3 = CU_ACC_EN_1

  // Notes on the sheet:
  //   LOAD/STORE
  //   JMPR
  //   JMP
  //   CLF
  //   FETCH CYCLE
  //   SELECT RESISTER
  //   ALU INSTRUCTION CYCLE
  //   DATA
  //   JXX
  //   NON-ALU INSTRUCTION CYCLE
endmodule
